# Fritzing sketch 433MHztransmitter (saved by Fritzing 0.9.3b)
breadboards: 1

parts:
  Part1 = BluePill
  U1 = FS1000A - 433Mhz RF Transmitter [package=THT]

nets:
  N1: Part1.3V31, U1.DATA
  GND3: Part1.GND3, U1.GND
  N2: Part1.B15, U1.VCC

custom parts:
  FS1000A - 433Mhz RF Transmitter: This is 433Mhz RF transmitter with receiver kit for Arduino ARM MCU wireless Application environment: Remote control switch, receiver module, motorcycles, automobile anti-theft products, home security products, electric doors, shutter doors, windows, remote control socket, remote control LED, remote audio remote control electric doors, garage door remote control, remote control retractable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
